// Logisim project cpu_logisim.circ as structural Verilog
module instruction_fetch (
  input  [15:0] pc_in
);

  wire decoder_1_out0, decoder_1_out1, decoder_1_out2, decoder_1_out3, decoder_1_out4, decoder_1_out5,
       decoder_1_out6, decoder_1_out7, decoder_1_out8, decoder_1_out9, decoder_1_out10, decoder_1_out11,
       decoder_1_out12, decoder_1_out13, decoder_1_out14, decoder_1_out15;
  wire [7:0] rom_1_p2;

  // ROM #(.addrWidth(15), .line("quad")) rom_1: pin names not known; wires that end beside it: pc_in[14:0], rom_1_p2
  Decoder #(.enable("false"), .select(4)) decoder_1 (
    .out0(decoder_1_out0), .out1(decoder_1_out1), .out2(decoder_1_out2), .out3(decoder_1_out3),
    .out4(decoder_1_out4), .out5(decoder_1_out5), .out6(decoder_1_out6), .out7(decoder_1_out7),
    .out8(decoder_1_out8), .out9(decoder_1_out9), .out10(decoder_1_out10), .out11(decoder_1_out11),
    .out12(decoder_1_out12), .out13(decoder_1_out13), .out14(decoder_1_out14), .out15(decoder_1_out15),
    .sel(rom_1_p2[3:0]));

  // Notes on the sheet:
  //   nop/singel operand
  //   ADD
  //   ADD
  //   ADD
  //   ADD
  //   ADD
  //   ADD
  //   ADD
  //   ADD
  //   ADD
  //   ADD
  //   ADD
  //   ADD
  //   ADD
  //   ADD
  //   ADD
endmodule
